# Fritzing sketch boat (saved by Fritzing 1.0.4)

parts:
  VCC = Header 3 [package=screwterminal-3.5mm-3_lock.007s]
  Ground = Header 3 [package=screwterminal-3.5mm-3_lock.007s]
  M5 = Dagu DGServo 9g (Top view) [part_number=RS001B]
  A1 = fs R6A
  Brushless_motor1 = Brushless Motor
  U1 = LIPO-11.1V-3 Cells [package=Li-Po-2200]
  ESC1 = ESC 30A
  Mod1 = Raspberry Pi Pico

nets:
  N1: VCC.1, M5.vcc
  N2: VCC.2, A1.Pin_2, A1.Pin_20
  N3: VCC.3, Mod1.pin_40
  N4: Ground.1, M5.gnd
  N5: Ground.2, A1.Pin_21
  N6: Ground.3, Mod1.pin_38, Mod1.pin_42
  N7: M5.pulse, Mod1.pin_1
  N8: A1.Pin_1, A1.Pin_19, Mod1.pin_4
  N9: Brushless_motor1.A, ESC1.A
  N10: Brushless_motor1.B, ESC1.B
  N11: Brushless_motor1.C, ESC1.C
  N12: U1.+, ESC1.V+
  N13: U1.-, ESC1.GND
  N14: ESC1.In, Mod1.pin_7

custom parts:
  fs R6A: FS R6A RC receiver.
  Brushless Motor: A standard Brushless DC motor
  LIPO-11.1V-3 Cells: Li-Po Battery-11.1V-3Cells-2200mAh
  ESC 30A: Electronic Speed Controller - 30A
  Raspberry Pi Pico: Raspberry Pi Pico. Based around the RP2040 microcontroller the Pico is a low cost microcontroller device bringing Raspberry Pi quality, cost, and easy of use to the microcontroller space. Jan 2021, Split part in to two versions: tht (this one) and SMD. This one will drill holes for a .1 in header in pcb to allow plugging in the module as well as providing pads to solder the module to the top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
